# Fritzing sketch UROV 2016 wiring (saved by Fritzing 0.9.2b)
breadboards: 2

parts:
  Part1 = Arduino Mega 2560 (Rev3)
  Part2 = Arduino Mega 2560 (Rev3)
  Part3 = 9 Degrees of Freedom - Sensor Stick  # not connected
  U1 = MAX485 [package=dil08]  # not connected
  MD09B1 = A4988 Stepper Motor Driver Carrier
  Power_plug1 = Power plug
  Pressure_sensor = IC, DIP package, 8 pins [chip_label=Pressure]

nets:
  GND: Part1.GND, Part2.GND, MD09B1.GROUND#141, Power_plug1.GND, Pressure_sensor.pin5, Pressure_sensor.pin6, Pressure_sensor.pin7, Pressure_sensor.pin8
  VIN: Part1.VIN, Part2.VIN, MD09B1.VMOT, Power_plug1.VCC
